# Fritzing sketch gaggia (saved by Fritzing 0.9.2b)
circuit board: 7.37872cm x 4.65147cm
breadboards: 1

parts:
  T2 = PNP-Transistor [package="TO92 [THT]"]
  Nano = Arduino Nano (Rev3.0)
  LED1 = Screw terminal - 2 pins [package=THT]
  Poti = screw terminal, 3 pins
  RTD = female pin header, 7 pins [form="♀ (female)"]
  OLED = screw terminal, 6 pins
  RELAY = Screw terminal - 2 pins [package=THT]
  LED2 = Screw terminal - 2 pins [package=THT]
  T1 = PNP-Transistor [package="TO92 [THT]"]
  12V = Screw terminal - 2 pins [package=THT]

nets:
  N1: T2.E, LED2.pin2
  N2: T2.B, Nano.D3
  N3: T2.C, LED2.pin1
  N4: Nano.GND, Poti.pin3, RTD.pin1, OLED.pin5, RELAY.pin2, 12V.pin2
  N5: Nano.D4, RELAY.pin1
  N6: Nano.D5, OLED.pin4
  N7: Nano.D6, OLED.pin3
  N8: Nano.D7, OLED.pin2
  N9: Nano.D8, OLED.pin1
  N10: Nano.D9, T1.B
  N11: Nano.D10, RTD.pin5
  N12: Nano.D11/MOSI, RTD.pin7
  N13: Nano.D12/MISO, RTD.pin4
  N14: Nano.VIN, 12V.pin1
  N15: Nano.5V, Poti.pin1, RTD.pin2, OLED.pin6
  N16: Nano.A0, Poti.pin2
  N17: Nano.D13/SCK, RTD.pin6
  N18: LED1.pin1, T1.C
  N19: LED1.pin2, T1.E

notes:
  tepeka.net / biglab.at
  gaggia cc controller v1.0
